# Fritzing sketch MouseTronix (saved by Fritzing 1.0.5)
breadboards: 6

parts:
  Part1 = Arduino Nano (Rev3.0) (ICSP)
  R1 = Resistor [tolerance=±5% resistance=150 package="0603 [SMD]"]
  LED1 = smd LED [color="Red (633nm)" current=20mA package="0805 [SMD]"]
  LED2 = smd LED [color="Yellow (592nm)" current=20mA package="0805 [SMD]"]
  LED3 = smd LED [color="Red (633nm)" current=20mA package="0805 [SMD]"]
  R3 = Resistor [tolerance=±5% resistance=150 package="0603 [SMD]"]
  LED4 = smd LED [color="Red (633nm)" current=20mA package="0805 [SMD]"]
  R4 = Resistor [tolerance=±5% resistance=150 package="0603 [SMD]"]
  LED5 = smd LED [color="Blue (430nm)" current=20mA package="0805 [SMD]"]
  LED6 = smd LED [color="Orange (612nm)" current=20mA package="0805 [SMD]"]
  LED7 = smd LED [color="Orange (612nm)" current=20mA package="0805 [SMD]"]
  R6 = Resistor [tolerance=±5% resistance=150 package="0603 [SMD]"]
  LED8 = smd LED [color="Red (660nm)" current=20mA package="0805 [SMD]"]
  LED9 = smd LED [color="Blue (430nm)" current=20mA package="0805 [SMD]"]
  LED10 = smd LED [color="Blue (430nm)" current=20mA package="0805 [SMD]"]
  R8 = Resistor [tolerance=±5% resistance=150 package="0603 [SMD]"]
  LED11 = smd LED [color="Orange (605nm)" current=20mA package="0805 [SMD]"]
  IC1 = SHIFT REGISTER [package=dil16]
  R9 = Resistor [tolerance=±5% resistance=50 package="0603 [SMD]"]
  R10 = Resistor [tolerance=±5% resistance=50 package="0603 [SMD]"]
  R11 = Resistor [tolerance=±5% resistance=50 package="0603 [SMD]"]
  R12 = Resistor [tolerance=±5% resistance=50 package="0603 [SMD]"]
  R13 = Resistor [tolerance=±5% resistance=50 package="0603 [SMD]"]
  R14 = Resistor [tolerance=±5% resistance=50 package="0603 [SMD]"]
  R15 = Resistor [tolerance=±5% resistance=50 package="0603 [SMD]"]
  R16 = Resistor [tolerance=±5% resistance=50 package="0603 [SMD]"]
  R17 = Resistor [tolerance=±5% resistance=50 package="0603 [SMD]"]
  R18 = Resistor [tolerance=±5% resistance=50 package="0603 [SMD]"]
  R19 = Resistor [tolerance=±5% resistance=50 package="0603 [SMD]"]
  R20 = Resistor [tolerance=±5% resistance=50 package="0603 [SMD]"]
  R21 = Resistor [tolerance=±5% resistance=50 package="0603 [SMD]"]
  R22 = Resistor [tolerance=±5% resistance=50 package="0603 [SMD]"]
  R23 = Resistor [tolerance=±5% resistance=50 package="0603 [SMD]"]
  R24 = Resistor [tolerance=±5% resistance=50 package="0603 [SMD]"]
  LED12 = smd LED [color="Yellow (592nm)" current=20mA package="0805 [SMD]"]
  LED13 = smd LED [color="Yellow (592nm)" current=20mA package="0805 [SMD]"]
  LED14 = smd LED [color="Yellow (592nm)" current=20mA package="0805 [SMD]"]
  LED15 = smd LED [color="Yellow (592nm)" current=20mA package="0805 [SMD]"]
  LED16 = smd LED [color="Yellow (592nm)" current=20mA package="0805 [SMD]"]
  LED17 = smd LED [color="Yellow (592nm)" current=20mA package="0805 [SMD]"]
  LED18 = smd LED [color="Yellow (592nm)" current=20mA package="0805 [SMD]"]
  LED19 = smd LED [color="Yellow (592nm)" current=20mA package="0805 [SMD]"]
  LED20 = smd LED [color="Yellow (592nm)" current=20mA package="0805 [SMD]"]
  LED21 = smd LED [color="Yellow (592nm)" current=20mA package="0805 [SMD]"]
  LED22 = smd LED [color="Yellow (592nm)" current=20mA package="0805 [SMD]"]
  LED23 = smd LED [color="Yellow (592nm)" current=20mA package="0805 [SMD]"]
  LED24 = smd LED [color="Yellow (592nm)" current=20mA package="0805 [SMD]"]
  LED25 = smd LED [color="Yellow (592nm)" current=20mA package="0805 [SMD]"]
  LED26 = smd LED [color="Yellow (592nm)" current=20mA package="0805 [SMD]"]
  LED27 = smd LED [color="Yellow (592nm)" current=20mA package="0805 [SMD]"]
  R25 = Resistor [tolerance=±5% resistance=50 package="0603 [SMD]"]
  R26 = Resistor [tolerance=±5% resistance=50 package="0603 [SMD]"]
  R27 = Resistor [tolerance=±5% resistance=50 package="0603 [SMD]"]
  R28 = Resistor [tolerance=±5% resistance=50 package="0603 [SMD]"]
  LED28 = smd LED [color="Yellow (592nm)" current=20mA package="0805 [SMD]"]
  LED29 = smd LED [color="Yellow (592nm)" current=20mA package="0805 [SMD]"]
  LED30 = smd LED [color="Orange (605nm)" current=20mA package="0805 [SMD]"]
  LED31 = smd LED [color="Orange (620nm)" current=20mA package="0805 [SMD]"]
  R29 = Resistor [tolerance=±5% resistance=50 package="0603 [SMD]"]
  R30 = Resistor [tolerance=±5% resistance=50 package="0603 [SMD]"]
  R31 = Resistor [tolerance=±5% resistance=50 package="0603 [SMD]"]
  R32 = Resistor [tolerance=±5% resistance=50 package="0603 [SMD]"]
  LED32 = smd LED [color="Yellow (592nm)" current=20mA package="0805 [SMD]"]
  LED33 = smd LED [color="Yellow (592nm)" current=20mA package="0805 [SMD]"]
  LED34 = smd LED [color="Yellow (592nm)" current=20mA package="0805 [SMD]"]
  LED35 = smd LED [color="Yellow (592nm)" current=20mA package="0805 [SMD]"]
  Part2 = Arduino Nano (Rev3.0) (ICSP)
  R33 = Resistor [tolerance=±5% resistance=150 package="0603 [SMD]"]
  R34 = Resistor [tolerance=±5% resistance=150 package="0603 [SMD]"]
  R35 = Resistor [tolerance=±5% resistance=150 package="0603 [SMD]"]
  R36 = Resistor [tolerance=±5% resistance=150 package="0603 [SMD]"]
  R37 = Resistor [tolerance=±5% resistance=150 package="0603 [SMD]"]
  R38 = Resistor [tolerance=±5% resistance=150 package="0603 [SMD]"]
  R39 = Resistor [tolerance=±5% resistance=150 package="0603 [SMD]"]
  R40 = Resistor [tolerance=±5% resistance=150 package="0603 [SMD]"]
  R41 = Resistor [tolerance=±5% resistance=150 package="0603 [SMD]"]
  R42 = Resistor [tolerance=±5% resistance=150 package="0603 [SMD]"]
  R43 = Resistor [tolerance=±5% resistance=150 package="0603 [SMD]"]
  R44 = Resistor [tolerance=±5% resistance=150 package="0603 [SMD]"]
  LED36 = smd LED [color="Blue (525nm)" current=20mA package="0805 [SMD]"]
  LED37 = smd LED [color="Orange (605nm)" current=20mA package="0805 [SMD]"]
  LED38 = smd LED [color="Red (633nm)" current=20mA package="0805 [SMD]"]
  LED39 = smd LED [color="Green (570nm)" current=20mA package="0805 [SMD]"]
  LED40 = smd LED [color="Blue (430nm)" current=20mA package="0805 [SMD]"]
  LED41 = smd LED [color="Blue (430nm)" current=20mA package="0805 [SMD]"]
  LED42 = smd LED [color="Blue (430nm)" current=20mA package="0805 [SMD]"]
  LED43 = smd LED [color="Red (660nm)" current=20mA package="0805 [SMD]"]
  LED44 = smd LED [color="Yellow (592nm)" current=20mA package="0805 [SMD]"]
  LED45 = smd LED [color="Orange (620nm)" current=20mA package="0805 [SMD]"]
  LED46 = smd LED [color="Yellow (592nm)" current=20mA package="0805 [SMD]"]
  LED47 = smd LED [color="Yellow (592nm)" current=20mA package="0805 [SMD]"]
  R45 = Resistor [tolerance=±5% resistance=150 package="0603 [SMD]"]
  R46 = Resistor [tolerance=±5% resistance=150 package="0603 [SMD]"]
  R47 = Resistor [tolerance=±5% resistance=150 package="0603 [SMD]"]
  R48 = Resistor [tolerance=±5% resistance=150 package="0603 [SMD]"]
  R49 = Resistor [tolerance=±5% resistance=150 package="0603 [SMD]"]
  R50 = Resistor [tolerance=±5% resistance=150 package="0603 [SMD]"]
  C1 = Electrolytic Capacitor [capacitance=100µF voltage=35V package="200 mil [THT, electrolytic]"]
  J1 = Basic Servo

nets:
  GND: Part1.GND, LED1.anode, LED2.anode, LED3.anode, LED4.anode, LED5.anode, LED6.anode, LED7.anode, LED8.anode, LED9.anode, LED10.anode, LED11.anode, IC1.GND, LED16.anode, LED17.anode, LED19.anode, LED20.anode, LED25.anode, LED27.anode, LED28.anode, LED29.anode, LED30.anode, LED31.anode, LED32.anode, LED33.anode, LED34.anode, LED35.anode, LED36.anode, LED37.anode, LED38.anode, LED39.anode, LED40.anode, LED41.anode, LED42.anode, LED43.anode, LED44.anode, LED45.anode, LED46.anode, LED47.anode, C1.-, J1.gnd
  N1: Part1.D2, IC1.SER
  N2: Part1.D3, IC1.RCK
  N3: Part1.D4, IC1.SCK
  N4: Part1.D5, R25.Pin_1
  N5: Part1.D6, R26.Pin_1
  N6: Part1.D7, R27.Pin_1
  N7: Part1.D8, R28.Pin_1
  N8: Part1.D9, R29.Pin_1
  N9: Part1.D10, R30.Pin_1
  N10: Part1.D11/MOSI, R31.Pin_1
  N11: Part1.D12/MISO, R32.Pin_1
  VCC: Part1.5V, IC1.SCL, IC1.G, IC1.VCC, C1.+, J1.vcc
  N12: Part1.A7, R8.Pin_0
  N13: Part1.A6, R45.Pin_0, R46.Pin_0
  N14: Part1.A5, R6.Pin_0
  N15: Part1.A4, R47.Pin_0, R48.Pin_0
  N16: Part1.A3, R4.Pin_0
  N17: Part1.A2, R49.Pin_0, R50.Pin_0
  N18: Part1.A1, R3.Pin_0
  N19: Part1.A0, R1.Pin_0
  N20: R1.Pin_1, LED1.cathode
  N21: LED2.cathode, R3.Pin_1
  N22: LED3.cathode, R50.Pin_1
  N23: LED4.cathode, R49.Pin_1
  N24: R4.Pin_1, LED5.cathode
  N25: LED6.cathode, R47.Pin_1
  N26: LED7.cathode, R48.Pin_1
  N27: R6.Pin_1, LED8.cathode
  N28: LED9.cathode, R46.Pin_1
  N29: LED10.cathode, R45.Pin_1
  N30: R8.Pin_1, LED11.cathode
  N31: IC1.QB, R11.Pin_1, R12.Pin_1
  N32: IC1.QC, R13.Pin_1, R14.Pin_1
  N33: IC1.QD, R15.Pin_1, R16.Pin_1
  N34: IC1.QE, R17.Pin_1, R18.Pin_1
  N35: IC1.QF, R19.Pin_1, R20.Pin_1
  N36: IC1.QG, R21.Pin_1, R22.Pin_1
  N37: IC1.QH, R23.Pin_1, R24.Pin_1
  N38: IC1.QA, R9.Pin_1, R10.Pin_1
  N39: R9.Pin_0, LED13.cathode
  N40: R10.Pin_0, LED12.cathode
  N41: R11.Pin_0, LED14.cathode
  N42: R12.Pin_0, LED15.cathode
  N43: R13.Pin_0, LED18.cathode
  N44: R14.Pin_0, LED17.cathode
  N45: R15.Pin_0, LED19.cathode
  N46: R16.Pin_0, LED16.cathode
  N47: R17.Pin_0, LED25.cathode
  N48: R18.Pin_0, LED24.cathode
  N49: R19.Pin_0, LED27.cathode
  N50: R20.Pin_0, LED20.cathode
  N51: R21.Pin_0, LED26.cathode
  N52: R22.Pin_0, LED22.cathode
  N53: R23.Pin_0, LED21.cathode
  N54: R24.Pin_0, LED23.cathode
  N55: LED12.anode, LED13.anode, LED14.anode, LED15.anode, LED18.anode
  N56: LED21.anode, LED22.anode, LED23.anode, LED24.anode, LED26.anode
  N57: R25.Pin_0, LED28.cathode
  N58: R26.Pin_0, LED29.cathode
  N59: R27.Pin_0, LED30.cathode
  N60: R28.Pin_0, LED31.cathode
  N61: R29.Pin_0, LED32.cathode
  N62: R30.Pin_0, LED33.cathode
  N63: R31.Pin_0, LED34.cathode
  N64: R32.Pin_0, LED35.cathode
  N65: Part2.D2, R44.Pin_0
  N66: Part2.D3, R43.Pin_0
  N67: Part2.D4, R42.Pin_0
  N68: Part2.D5, R41.Pin_0
  N69: Part2.D9, J1.pulse
  N70: Part2.A7, R33.Pin_0
  N71: Part2.A6, R34.Pin_0
  N72: Part2.A5, R35.Pin_0
  N73: Part2.A4, R36.Pin_0
  N74: Part2.A3, R37.Pin_0
  N75: Part2.A2, R38.Pin_0
  N76: Part2.A1, R39.Pin_0
  N77: Part2.A0, R40.Pin_0
  N78: R33.Pin_1, LED36.cathode
  N79: R34.Pin_1, LED37.cathode
  N80: R35.Pin_1, LED38.cathode
  N81: R36.Pin_1, LED39.cathode
  N82: R37.Pin_1, LED40.cathode
  N83: R38.Pin_1, LED41.cathode
  N84: R39.Pin_1, LED42.cathode
  N85: R40.Pin_1, LED43.cathode
  N86: R41.Pin_1, LED47.cathode
  N87: R42.Pin_1, LED44.cathode
  N88: R43.Pin_1, LED46.cathode
  N89: R44.Pin_1, LED45.cathode

// code stored in the sketch: MouseTronix_Arduino1.ino
//**************************************************************//
//  Name    : First 8 LEDs Test
//  Author  : Griffin Moede
//  Date    : 7 Sep 2025
//  Version : 1.0
//  Notes   : Prototyping LED circuit for shadowbox
//****************************************************************
// #define planeHit0 A0
// #define planeHit1 A1
// #define planeHit2 A2
// #define planeHit3 A3
// #define planeHit4 A4
// #define planeHit5 A5
// #define planeHit6 A6
// #define planeHit7 A7


static const int planeHits[] = {A0, A1, A2, A3, A4, A5, 11, 12};


static const int planeLightPatternsLength = 6;


static int maxBrightness = 255;
static int minBrightness = 0;


//PIN DEFINITIONS
static const int hangGliderPin = 3;
static const int mouseBodyPin = 5;
static const int planeLLPin = 4;
static const int planeLRPin = 7;
static const int planeRLPin = 8;
static const int planeRRPin = 10;
static const int heliEyesPin = 9;



int hangGliderBrightness = 51;
int hangGliderFadeAmount = 4;
int mouseBodyBrightness = maxBrightness;
int mouseBodyFadeAmount = 6;


int heliEyesBrightness = 90;
int heliEyesFadeAmount = 15;


int planeLightPhase = 1;


int gunSequenceDelayOne = 1500;
int gunSequenceDelayTwo = 500;
int gunClock = 0;


int planeLights[] = { planeLLPin, planeLRPin, planeRLPin, planeRRPin };
int planeLightPattern0[] = { 0, 0, 0, 0, 0, 0, 0, 0 };
int planeLightStep = 0;
int planeLightPattern = 0;
int planeLightPattern1[] = { 0b00001001, 0b00000110, 0b00001001, 0b00000110,0b00001001, 0b00000110,0b00001001, 0b00000110};
int planeLightPattern2[] = { 0b00001000, 0b00000100, 0b00000010, 0b00000001, 0b00001000, 0b00000100, 0b00000010, 0b00000001};
int planeLightPattern3[] = { 0b00001001, 0b00000000, 0b00001001, 0b00000000, 0b00001001, 0b00000000, 0b00001001, 0b00000000};
int planeLightPattern4[] = { 0b00000110, 0b00000000, 0b00000110, 0b00000000, 0b00000110, 0b00000000, 0b00000110, 0b00000000};
int planeLightPattern5[] = { 0b00001000, 0b00000100, 0b00000010, 0b00000001, 0b00000001, 0b00000010, 0b00000100, 0b00001000};
int* planeLightPatterns[planeLightPatternsLength] = { planeLightPattern0, planeLightPattern1 , planeLightPattern2, planeLightPattern3, planeLightPattern4, planeLightPattern5};
bool shouldChooseNextPlaneLightPhase = true;




void setup() {
  Serial.begin(9600);
  pinMode(hangGliderPin, OUTPUT);
  pinMode(mouseBodyPin, OUTPUT);
  pinMode(planeLLPin, OUTPUT);
  pinMode(planeLRPin, OUTPUT);
  pinMode(planeRLPin, OUTPUT);
  pinMode(planeRRPin, OUTPUT);
  pinMode(heliEyesPin, OUTPUT);


  for(int i = 0; i < 8; i++){
    pinMode(planeHits[i], OUTPUT);
  }
}


void loop() {
  //digitalWrite(latchPin, );
  // pause before next value:
  analogWrite(hangGliderPin, hangGliderBrightness);
  analogWrite(mouseBodyPin, mouseBodyBrightness);
  analogWrite(heliEyesPin, heliEyesBrightness);
  fade(hangGliderPin, hangGliderFadeAmount, hangGliderBrightness);
  fade(mouseBodyPin, mouseBodyFadeAmount, mouseBodyBrightness);
  fade(heliEyesPin, heliEyesFadeAmount, heliEyesBrightness);
  shootPlaneGuns();


  delay(75);
}


void shootPlaneGuns() {
  if(planeLightStep >= 8){
    int randomNumber = random(0, planeLightPatternsLength);
    Serial.println(randomNumber);
    planeLightPattern =  randomNumber;
    planeLightStep = 0;
  }
  int planeLightPatternInteger = planeLightPatterns[planeLightPattern][planeLightStep];
  writePlaneLights(planeLightPatternInteger);
  planeLightStep++;


  // if(shouldChooseNextPlaneLightPhase){
  //   shouldChooseNextPlaneLightPhase = false;
  //   int randomNumber = random(0, planeLightPatternsLength);
  //   Serial.println(randomNumber);
  //   planeLightPattern =  randomNumber;
  //   planeLightStep = 0;
  // }
}


void writePlaneLights(int planeLightPatternInteger){
    digitalWrite(planeLLPin, planeLightPatternInteger & 0b1000);
    digitalWrite(planeLRPin, planeLightPatternInteger & 0b0100);
    digitalWrite(planeRLPin, planeLightPatternInteger & 0b0010);
    digitalWrite(planeRRPin, planeLightPatternInteger & 0b0001);
      for(int i = 0; i < 8; i++){
        if(planeLightPatternInteger!= 0 && i == planeLightStep){
          digitalWrite(planeHits[i], HIGH);
        } else {
          digitalWrite(planeHits[i], LOW);
        }
      }
    
}


// the loop routine runs over and over again forever:
void fade(int pin, int &fadeAmount, int &brightness) {
  // set the brightness of pin 9:
  // change the brightness for next time through the loop:
  brightness = brightness + fadeAmount;


  // reverse the direction of the fading at the ends of the fade:
  if (brightness <= 0) {
    brightness = 0;
    fadeAmount = -fadeAmount;
  } else if (brightness >= 255) {
    brightness = 255;
    fadeAmount = -fadeAmount;
  }
}
